# Fritzing sketch Wiring (saved by Fritzing 0.9.3b)
breadboards: 1

parts:
  Часть1 = Arduino Uno (Rev3)
  DS220 = LM35 Temperature Sensor [thermistor_type=NTC package="TO92 [THT]"]
  Door_status_sensor = Pushbutton [package="[THT]"]
  R1 = Resistor [tolerance=±5% resistance=10k package=THT]

nets:
  N1: Часть1.D2, DS220.Vout
  N2: Часть1.D3_PWM, Door_status_sensor.Pin_1, Door_status_sensor.Pin_2, R1.Pin_0
  N3: Часть1.5V, DS220.+Vs, Door_status_sensor.Pin_3, Door_status_sensor.Pin_4
  GND: Часть1.GND, DS220.GND, R1.Pin_1
